# Fritzing sketch Untitled-Sketch-2 (saved by Fritzing 0.9.3b)
breadboards: 1

parts:
  元件1 = Arduino Uno (Rev3)
  LED1 = smd LED [color="Red (633nm)" package="0805 [SMD]"]
  LED2 = smd LED [color="Red (633nm)" package="1206 [SMD]"]

nets:
  N1: 元件1.D12/MISO, LED2.anode
  N2: 元件1.D13/SCK, LED1.anode
  N3: 元件1.GND, LED1.cathode, LED2.cathode
